# Fritzing sketch Esquematico_v1 (saved by Fritzing 0.9.3b)
breadboards: 1

parts:
  A1 = Raspberry Pi Pico W
  S1 = H-Bridge with L298N
  U1 = LM2596 step down module
  Mod1 = KY-024 Linear Hall Magnetic Sensor Module [package="Breakout board"]
  L1 = Solenoid
  L2 = Solenoid

nets:
  N1: A1.pin_3, A1.pin_8, A1.pin_13, A1.pin_18, A1.pin_23, A1.pin_28, A1.pin_33, A1.pin_38, S1.GND, U1.IN-, U1.OUT-, Mod1.G
  N2: A1.pin_21, S1.IN2
  N3: A1.pin_29, Mod1.A0
  N4: A1.pin_39, U1.IN+, Mod1.+
  N5: S1.12V, U1.OUT+
  N6: S1.M1-01, L1.pin2, L2.pin2
  N7: S1.M1-02, L1.pin1, L2.pin1

custom parts:
  Raspberry Pi Pico W: Raspberry Pi Pico W. Based around the RP2040 microcontroller the Pico W is a low cost microcontroller device bringing Raspberry Pi quality, cost, and easy of use to the microcontroller space. The areas marked KEEPOUT in pcb silkscreen should not have traces running through them to avoid shorts on a soldered in module!
  H-Bridge with L298N: h-bridge
  LM2596 step down module: LM2596 DC-DC step down power supply module 3 A.
  KY-024 Linear Hall Magnetic Sensor Module: KY-024 Linear Hall Magnetic Sensor Module reacts iin the presence of a magnetic field.
